# Fritzing sketch boat_response_wiring (saved by Fritzing 0.9.3b)
breadboards: 1

parts:
  Part1 = Arduino Uno (Rev3) - ICSP
  Part2 = NRF24L01+ Breakout Board
  S1 = H-Bridge with L298N
  R1 = PHOTOCELL [package=photocell-kit]
  U1 = TMP36 [package=to-92]
  M1 = DC Motor
  M2 = DC Motor
  VCC1 = Battery
  R2 = Resistor [tolerance=±5% resistance=220 package="0805 [SMD]"]

nets:
  N1: Part1.A0, R1.P$2, R2.Pin_0
  N2: Part1.A1, U1.VOUT
  N3: Part1.ICSP_MISO, Part1.D12/MISO, Part2.MISO
  N4: Part1.ICSP_MOSI, Part1.D11_PWM/MOSI, Part2.MOSI
  N5: Part1.D8, Part2.CS
  N6: Part1.D9_PWM, S1.IN4
  N7: Part1.D10_PWM/SS, S1.IN3
  N8: Part1.D13/SCK, Part2.SCK
  GND: Part1.GND, Part2.GND, U1.GND, R2.Pin_1
  N9: Part1.D3_PWM, S1.IN2
  N10: Part1.D4, S1.IN1
  N11: Part1.D5_PWM, S1.ENB
  N12: Part1.D6_PWM, S1.ENA
  N13: Part1.D7, Part2.CE
  3V3: Part1.3V3, Part2.VCC
  5V: Part1.5V, R1.P$1, U1.VCC
  VIN: Part1.VIN, S1.5V
  N14: S1.12V, VCC1.+
  N15: S1.GND, VCC1.-
  N16: S1.M1-01, M1.pin_1
  N17: S1.M1-02, M1.pin_2
  N18: S1.M2-01, M2.pin_2
  N19: S1.M2-02, M2.pin_1

custom parts:
  H-Bridge with L298N: h-bridge
