# Fritzing sketch user_controls_wiring (saved by Fritzing 0.9.3b)

parts:
  Part1 = Arduino Uno (Rev3) - ICSP
  Part2 = NRF24L01+ Breakout Board
  Part3 = Thumb Joystick

nets:
  N1: Part1.A0, Part3.VERT
  N2: Part1.A1, Part3.HORZ
  N3: Part1.ICSP_MISO, Part1.D12/MISO, Part2.MISO
  N4: Part1.ICSP_MOSI, Part1.D11_PWM/MOSI, Part2.MOSI
  N5: Part1.D8, Part2.CS
  N6: Part1.D13/SCK, Part2.SCK
  GND: Part1.GND, Part2.GND, Part3.GND
  N7: Part1.D7, Part2.CE
  3V3: Part1.3V3, Part2.VCC
  5V: Part1.5V, Part3.VCC
